# Fritzing sketch arduino_mini_pro (saved by Fritzing 0.9.3b)
circuit board: 6.84986cm x 4.61896cm
breadboards: 1

parts:
  パーツ1 = Arduino Pro Mini (3.3V)
  U1 = TA7291P [package=HSIP10-P-2.54(THT)]
  U2 = TA7291P [package=HSIP10-P-2.54(THT)]
  M1 = DC Motor
  M2 = DC Motor
  LED1 = LED - 5mm [color="Red (633nm)" package="5 mm [THT]"]
  R1 = Resistor [tolerance=±5% resistance=1k package=THT]
  R2 = Resistor [tolerance=±5% resistance=1k package=THT]
  R3 = Resistor [tolerance=±5% resistance=1k package=THT]
  LED2 = LED - 5mm [color="Red (633nm)" package="5 mm [THT]"]
  R4 = Photocell (LDR) [package=THT]
  VCC1 = Battery
  R5 = Resistor [tolerance=±5% resistance=0 package=THT]
  DC-IN = Resistor [tolerance=±5% resistance=0 package=THT]
  DC-OUT = Resistor [tolerance=±5% resistance=0 package=THT]

nets:
  GND: パーツ1.GND, U1.GND, U2.GND, LED1.cathode, LED2.cathode, R4.pin_1, VCC1.-, DC-IN.Pin_1, DC-OUT.Pin_1
  N1: パーツ1.RAW, DC-OUT.Pin_0
  N2: パーツ1.VCC, R1.Pin_0
  N3: パーツ1.A2, R2.Pin_0
  N4: パーツ1.A1, R3.Pin_0
  N5: パーツ1.A0, R1.Pin_1, R4.pin_0
  N6: パーツ1.D7, U1.IN2
  N7: パーツ1.D6, U1.Vref
  N8: パーツ1.D5, U1.IN1
  N9: パーツ1.D4, U2.IN2
  N10: パーツ1.D3, U2.Vref
  N11: パーツ1.D2, U2.IN1
  N12: U1.OUT1, M1.pin_2
  VCC: U1.Vcc, U1.Vs, U2.Vcc, U2.Vs, R5.Pin_0
  N13: U1.OUT2, M1.pin_1
  N14: U2.OUT1, M2.pin_2
  N15: U2.OUT2, M2.pin_1
  N16: LED1.anode, R2.Pin_1
  N17: R3.Pin_1, LED2.anode
  N18: VCC1.+, R5.Pin_1, DC-IN.Pin_0

notes:
  igapon@gmail.com

custom parts:
  TA7291P: The IC are Full-Bridge Driver. 4 modes available (CW / CCW / STOP / BRAKE) and PWM control. Output current:1.0 A (AVE.) 2.0 A (PEAK)
