# Fritzing sketch arduino_uno (saved by Fritzing 0.9.3b)
circuit board: 5.33154cm x 5.16346cm
breadboards: 1

parts:
  TA7791P = TA7291P [package=HSIP10-P-2.54(THT)]
  M1 = DC Motor
  M2 = DC Motor
  LED1 = LED - 5mm [color="Red (633nm)" package="5 mm [THT]"]
  R1 = Resistor [tolerance=±5% resistance=1k package=THT]
  R2 = Resistor [tolerance=±5% resistance=1k package=THT]
  R3 = Resistor [tolerance=±5% resistance=1k package=THT]
  LED2 = LED - 5mm [color="Red (633nm)" package="5 mm [THT]"]
  VCC2(7-12V) = Battery block 9V
  パーツ1 = Arduino Uno (Rev3)
  TA7791P_2 = TA7291P [package=HSIP10-P-2.54(THT)]
  R4-opt = Photocell (LDR) [package=THT]
  R5 = Resistor [tolerance=±5% resistance=0 package=THT]
  VCC1(4_75-5_25V) = Electrolytic Capacitor [capacitance=1µF package="100 mil [THT, electrolytic]"]
  VCC3(5_25-7V) = Battery

nets:
  GND: TA7791P.GND, LED1.cathode, LED2.cathode, VCC2(7-12V).-, パーツ1.GND, TA7791P_2.GND, R4-opt.pin_1, VCC1(4_75-5_25V).-, VCC3(5_25-7V).-
  N1: TA7791P.OUT1, M2.pin_2
  N2: TA7791P.Vref, パーツ1.D3_PWM
  N3: TA7791P.IN1, パーツ1.D2
  N4: TA7791P.IN2, パーツ1.D4
  VCC: TA7791P.Vcc, TA7791P.Vs, TA7791P_2.Vcc, TA7791P_2.Vs, R5.Pin_0, VCC3(5_25-7V).+
  N5: TA7791P.OUT2, M2.pin_1
  N6: M1.pin_1, TA7791P_2.OUT2
  N7: M1.pin_2, TA7791P_2.OUT1
  N8: LED1.anode, R2.Pin_1
  N9: R1.Pin_0, パーツ1.5V, VCC1(4_75-5_25V).+
  N10: R1.Pin_1, パーツ1.A0, R4-opt.pin_0
  N11: R2.Pin_0, パーツ1.A2
  N12: R3.Pin_0, LED2.anode
  N13: R3.Pin_1, パーツ1.A1
  N14: VCC2(7-12V).+, パーツ1.VIN, R5.Pin_1
  N15: パーツ1.D5_PWM, TA7791P_2.IN1
  N16: パーツ1.D6_PWM, TA7791P_2.Vref
  N17: パーツ1.D7, TA7791P_2.IN2

notes:
  igapon@gmail.com

custom parts:
  TA7291P: The IC are Full-Bridge Driver. 4 modes available (CW / CCW / STOP / BRAKE) and PWM control. Output current:1.0 A (AVE.) 2.0 A (PEAK)
